# Fritzing sketch diagrama (saved by Fritzing 0.9.6b)
breadboards: 1

parts:
  U1 = NodeMCU V3.0
  microSD1 = MicroSD Card Module
  S1 = Pushbutton [package="[THT]"]

nets:
  N1: U1.D2, S1.Pin_1, S1.Pin_2
  3V3: U1.3V3, microSD1.VCC
  N2: U1.D5, microSD1.SCK
  N3: U1.D6, microSD1.MISO
  N4: U1.D7, microSD1.MOSI
  N5: U1.D8, microSD1.CS
  N6: U1.GND#13, microSD1.GND
  N7: U1.GND#41, S1.Pin_3, S1.Pin_4

notes:
  GND
  3.3V
  MISO
  MOSI
  SCK
  CS

custom parts:
  NodeMCU V3.0: ESP8266 based NodeMCU
